# Fritzing sketch Clock (saved by Fritzing 0.9.3b)
circuit board: 6cm x 4cm

parts:
  ESP-01 = ESP8266 WiFi Module [part_number=ESP8266]
  DC_DC_Converter_->5V = RioRand LM2596
  470Ohm = Resistor [tolerance=±5% resistance=470 package=THT]
  470Ohm_2 = Resistor [tolerance=±10% resistance=470 package=THT]
  LED1 = LED - 5mm [color="Red (633nm)" package="5 mm [THT]"]
  ->WS2812B = Screw terminal - 3 pins [package=THT]
  LVL_Shifter = Level Shifter
  J1 = female alternating pin header, 4 pins [form="♀ (female)"]
  J2 = female alternating pin header, 4 pins [form="♀ (female)"]
  PWR = Screw terminal - 2 pins [package=THT]
  C1 = Electrolytic Capacitor [capacitance=1000µF package="300 mil [THT, electrolytic]"]

nets:
  N1: ESP-01.RXD, LVL_Shifter.LV1
  N2: ESP-01.VCC, ESP-01.CH_PD, LVL_Shifter.3V
  N3: ESP-01.GPIO_0, LVL_Shifter.LV2
  N4: ESP-01.GPIO_2, LVL_Shifter.LV3
  GND: ESP-01.GND, DC_DC_Converter_->5V.Pin_2, DC_DC_Converter_->5V.Pin_4, LED1.anode, ->WS2812B.GND, LVL_Shifter.GND, PWR.pin1, C1.-
  N5: ESP-01.TXD, LVL_Shifter.LV4
  N6: DC_DC_Converter_->5V.Pin_1, PWR.pin2
  VIN: DC_DC_Converter_->5V.Pin_3, ->WS2812B.Vin, LVL_Shifter.5V, C1.+
  N7: 470Ohm.Pin_0, J1.pin1
  N8: 470Ohm.Pin_1, LED1.cathode
  N9: 470Ohm_2.Pin_0, J1.pin3
  N10: 470Ohm_2.Pin_1, ->WS2812B.Data
  N11: LVL_Shifter.HV4, J2.pin1
  N12: LVL_Shifter.HV3, J2.pin2
  N13: LVL_Shifter.HV2, J2.pin3
  N14: LVL_Shifter.HV1, J2.pin4

custom parts:
  ESP8266 WiFi Module: Generic WiFi Module based on the ESP8266 with onboard PCB antenna and UART communications
  Screw terminal - 3 pins: Screw terminal with 3 pins
  Level Shifter: Level Shifter 5V/3V
